# Fritzing sketch FreeRTOS_led (saved by Fritzing 0.9.3b)
breadboards: 1

parts:
  Part1 = Arduino Uno (Rev3)
  LED1 = LED - 5mm [color="Red (633nm)" package="5 mm [THT]"]
  LED2 = LED - 5mm [color="Yellow (592nm)" package="5 mm [THT]"]
  LED3 = LED - 5mm [color="Green (565nm)" package="5 mm [THT]"]
  R1 = Resistor [tolerance=±5% resistance=220 package=THT]
  R2 = Resistor [tolerance=±5% resistance=220 package=THT]
  R3 = Resistor [tolerance=±5% resistance=220 package=THT]

nets:
  N1: Part1.GND, R1.Pin_0, R2.Pin_0, R3.Pin_0
  N2: Part1.D3_PWM, LED2.anode
  N3: Part1.D4, LED1.anode
  N4: Part1.D5_PWM, LED3.anode
  N5: LED1.cathode, R2.Pin_1
  N6: LED2.cathode, R1.Pin_1
  N7: LED3.cathode, R3.Pin_1
